# Fritzing sketch work-status-board (saved by Fritzing 0.9.3b)
circuit board: 8.46667cm x 5.64444cm
breadboards: 1

parts:
  R1 = Resistor [tolerance=±5% resistance=220 package=THT]
  R2 = Resistor [tolerance=±5% resistance=220 package=THT]
  R3 = Resistor [tolerance=±5% resistance=220 package=THT]
  R4 = Resistor [tolerance=±5% resistance=220 package=THT]
  LED1 = LED - 5mm [color="Red (633nm)" package="5 mm [THT]"]
  LED2 = LED - 5mm [color="Orange (605nm)" package="5 mm [THT]"]
  LED3 = LED - 5mm [color="Yellow (574nm)" package="5 mm [THT]"]
  LED4 = LED - 5mm [color="Green (555nm)" package="5 mm [THT]"]
  Part1 = Arduino Uno (Rev3)

nets:
  N1: R1.Pin_0, Part1.D10_PWM/SS
  N2: R1.Pin_1, LED1.cathode
  N3: R2.Pin_0, Part1.D11_PWM/MOSI
  N4: R2.Pin_1, LED2.cathode
  N5: R3.Pin_0, Part1.D12/MISO
  N6: R3.Pin_1, LED3.cathode
  N7: R4.Pin_0, Part1.D13/SCK
  N8: R4.Pin_1, LED4.cathode
  N9: LED1.anode, LED2.anode, LED3.anode, LED4.anode, Part1.GND
